# Fritzing sketch Zeittafel (saved by Fritzing 1.0.4)
breadboards: 1

parts:
  A1 = Hiletgo 8digit led display
  Bauteil1 = Arduino Nano (Rev3.0) (ICSP)
  M3 = fc-51 [package=THT]
  M4 = fc-51 [package=THT]

nets:
  N1: A1.Pin_1, A1.Pin_10, Bauteil1.5V, M3.pin3, M4.pin3
  N2: A1.Pin_2, A1.Pin_9, Bauteil1.GND, M3.pin2, M4.pin2
  N3: A1.Pin_3, Bauteil1.D7
  N4: A1.Pin_4, Bauteil1.D6
  N5: A1.Pin_5, A1.Pin_6, Bauteil1.D5
  N6: Bauteil1.D2, M4.pin1
  N7: Bauteil1.D3, M3.pin1

custom parts:
  Hiletgo 8digit led display: MAX7219 is an integrated serial input / output common-cathode display driver, which connects your microprocessor to a 7-segment digital LED display with 8 digits.
